# Fritzing sketch board (saved by Fritzing 0.9.3b)
breadboards: 3

parts:
  Part1 = Arduino Uno (Rev3)
  Part3 = RFID-RC522-v2  # not connected
  R1 = Resistor [tolerance=±5% resistance=220 package=THT]  # not connected
  R2 = Trimmer Potentiometer [maximum_resistance=10kΩ package=THT]  # not connected
  LED1 = LED - 5mm [color="Red (633nm)" package="5 mm [THT]"]  # not connected
  U1 = 74HC595 [package="DIP16 [THT]"]  # not connected
  J1 = Basic Servo  # not connected
  LCD1 = LCD screen

nets:
  N1: Part1.D8, LCD1.DB7
  N2: Part1.D3_PWM, LCD1.RS
  N3: Part1.D4, LCD1.E
  N4: Part1.D5_PWM, LCD1.DB4
  N5: Part1.D6_PWM, LCD1.DB5
  N6: Part1.D7, LCD1.DB6
  5V: Part1.5V, LCD1.VDD, LCD1.LED+
  GND: Part1.GND, LCD1.VSS, LCD1.R/W, LCD1.LED-

custom parts:
  RFID-RC522-v2: A simple China made RFID-RC522 Reader; do check the pin labels, as this is a MFRC522 based clone.
